# Fritzing sketch Schematic (saved by Fritzing 0.9.5d)
breadboards: 1

parts:
  R1 = Resistor [tolerance=±5% resistance=10k package=THT]
  R2 = Resistor [tolerance=±5% resistance=100 package=THT]
  D1 = LTE-302 [part_number=IR-LED package=lte-302]
  Q1 = LTR-301 [part_number="Short + / Long GND" package=ltr-301]
  A1 = ESP32 DevKitc V4
  LED1 = LED - 5mm [color="Green (565nm)" package="5 mm [THT]"]
  R3 = Resistor [tolerance=±5% resistance=150 package=THT]

nets:
  N1: R1.Pin_0, A1.Pin_1
  N2: R1.Pin_1, Q1.C, A1.Pin_37
  N3: R2.Pin_0, A1.Pin_31
  N4: R2.Pin_1, D1.C
  N5: Q1.E, A1.Pin_32, LED1.cathode
  N6: A1.Pin_30, R3.Pin_0
  N7: LED1.anode, R3.Pin_1

custom parts:
  ESP32 DevKitc V4: ESP32-DevKitC board with ESP32-WROOM-32 module. ESP32-DevKitC V4 is a small-sized ESP32-based development board produced by Espressif. Most of the pins on the ESP module are broken out to the pin headers on the board. The pins D0, D1, D2, D3, CMD and CLK are used internally for communication between ESP32 and SPI flash memory. They are grouped on both sides near the USB connector. Avoid using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
